# Fritzing sketch CAN bus (saved by Fritzing 0.9.10b)
breadboards: 1

parts:
  LCD1 = LCD screen
  Part1 = Arduino Uno (Rev3)
  Part2 = Arduino Nano (Rev3.0)
  M1 = Niren can bus module [package=THT]
  M2 = Niren can bus module [package=THT]
  HC-SR04_Sensor_1 = HC-SR04 Ultrasonic Distance Sensor
  R1 = Trimmer Potentiometer [maximum_resistance=10kΩ knob_status=50% power=0.5W package=THT]
  R2 = Resistor [tolerance=±5% resistance=220 package="0805 [SMD]"]

nets:
  VSS: LCD1.VSS, LCD1.R/W, LCD1.LED-, Part1.GND, M1.pin2, R1.leg2
  VDD: LCD1.VDD, Part1.5V, M1.pin1, R1.leg1, R2.Pin_1
  N1: LCD1.V0, R1.wiper
  N2: LCD1.RS, Part1.D8
  N3: LCD1.E, Part1.D7
  N4: LCD1.DB4, Part1.D5_PWM
  N5: LCD1.DB5, Part1.D4
  N6: LCD1.DB6, Part1.D3_PWM
  N7: LCD1.DB7, Part1.D2
  N8: LCD1.LED+, R2.Pin_0
  N9: Part1.D10_PWM/SS, M1.pin3
  N10: Part1.D11_PWM/MOSI, M1.pin5
  N11: Part1.D12/MISO, M1.pin4
  N12: Part1.D13/SCK, M1.pin6
  N13: Part2.D5, HC-SR04_Sensor_1.TRIG, HC-SR04_Sensor_1.ECHO
  N14: Part2.D10, M2.pin3
  N15: Part2.D11/MOSI, M2.pin5
  N16: Part2.D12/MISO, M2.pin4
  GND: Part2.GND, M2.pin2, HC-SR04_Sensor_1.GND
  5V: Part2.5V, M2.pin1, HC-SR04_Sensor_1.VCC
  N17: Part2.D13/SCK, M2.pin6
  N18: M1.pin10, M1.pin12, M2.pin10
  N19: M1.pin11, M1.pin13, M2.pin11

custom parts:
  Niren can bus module: Niren can bus module availabe on ebay and others. Pcb view assumes that you unsolder the 7 pin header and resolder it on the bottom of the module to connect to the pcb. The two jumpers and the can bus connector remain on the top of the board and don't appear in pcb view.
